// Logisim project CPU2.circ as structural Verilog: 1 circuit, main circuit main
module main (
);

  wire PROG_REG_WRITE;
  wire [2:0] PROG_REG_ADDR;
  wire [15:0] counter_1_q;
  wire [31:0] PROG_data;

  ROM #(.addrWidth(16), .dataWidth(32)) PROG (.addr(counter_1_q), .data(PROG_data));
  Counter #(.width(16), .max('hffff)) counter_1 (.Q(counter_1_q));  // open: clr, load, up, count, clk, D, carry
  Register #(.width(32)) IR (.D(PROG_data));  // open: en, clk, Q, clr
  // Register_Bank #(.width(32), .registerCount(8), .portCount(1)) register_bank_1: pin names not known; wires that end beside it: PROG_REG_ADDR, PROG_REG_WRITE, PROG_data
endmodule
